// Logisim project Symple electronic security system.circ as structural Verilog: 3 circuits, main circuit main
module main (
  input  in_1,
  input  in_2,
  output out_3
);

  wire and_1_out, and_2_out, not_1_out, not_2_out;

  not not_1 (not_1_out, in_1);
  not not_2 (not_2_out, in_2);
  and and_1 (and_1_out, not_1_out, in_2);
  and and_2 (and_2_out, in_1, not_2_out);
  or or_1 (out_3, and_1_out, and_2_out);
endmodule

module XOR_Circuit (
  input  in_1,
  input  in_2
);

  wire and_1_out, and_2_out, not_1_out, not_2_out, or_1_out;

  not not_1 (not_1_out, in_1);
  not not_2 (not_2_out, in_2);
  and and_1 (and_1_out, not_1_out, in_2);
  and and_2 (and_2_out, in_1, not_2_out);
  LED led_1 (.in(or_1_out));
  or or_1 (or_1_out, and_1_out, and_2_out);
endmodule

module Simple_electronic_security_system (
  input  [3:0] Input_code,
  input  [3:0] Predefined_code
);

  wire _0_out, _1_out, _2_out, _3_out, _4_out, _5_out, _6_out, _7_out, _8_out, _9_out, A_out, and_1_out,
       B_out, C_out, comparator_1_gt, comparator_1_lt, controlled_buffer_1_out, controlled_buffer_2_out,
       controlled_buffer_3_out, controlled_buffer_4_out, D_out, decoder_1_out0, decoder_1_out1,
       decoder_2_out1, decoder_3_out0, demultiplexer_1_out0, demultiplexer_1_out1, demultiplexer_1_out2,
       demultiplexer_1_out3, E_out, F_out, multiplexer_1_out, multiplexer_2_out, multiplexer_3_out,
       not_1_out, undriven, undriven_2, undriven_3, undriven_4;
  wire [1:0] decoder_3_out1;
  wire [7:4] undriven_5, undriven_6;

  Button _0 (.out(_0_out));
  Button _4 (.out(_4_out));
  Button _8 (.out(_8_out));
  Button C (.out(C_out));
  assign controlled_buffer_1_out = undriven ? _0_out : 1'bz;  // Controlled_Buffer controlled_buffer_1
  Button _1 (.out(_1_out));
  assign controlled_buffer_2_out = undriven ? _4_out : 1'bz;  // Controlled_Buffer controlled_buffer_2
  Button _5 (.out(_5_out));
  Button _9 (.out(_9_out));
  assign controlled_buffer_3_out = undriven ? _8_out : 1'bz;  // Controlled_Buffer controlled_buffer_3
  assign controlled_buffer_4_out = undriven ? C_out : 1'bz;  // Controlled_Buffer controlled_buffer_4
  Button D (.out(D_out));
  Button _2 (.out(_2_out));
  assign controlled_buffer_1_out = undriven_2 ? _1_out : 1'bz;  // Controlled_Buffer controlled_buffer_5
  assign controlled_buffer_2_out = undriven_2 ? _5_out : 1'bz;  // Controlled_Buffer controlled_buffer_6
  Button _6 (.out(_6_out));
  Button A (.out(A_out));
  assign controlled_buffer_3_out = undriven_2 ? _9_out : 1'bz;  // Controlled_Buffer controlled_buffer_7
  assign controlled_buffer_4_out = undriven_2 ? D_out : 1'bz;  // Controlled_Buffer controlled_buffer_8
  Button E (.out(E_out));
  assign controlled_buffer_1_out = undriven_3 ? _2_out : 1'bz;  // Controlled_Buffer controlled_buffer_9
  Button _3 (.out(_3_out));
  assign controlled_buffer_2_out = undriven_3 ? _6_out : 1'bz;  // Controlled_Buffer controlled_buffer_10
  Button _7 (.out(_7_out));
  Button B (.out(B_out));
  assign controlled_buffer_3_out = undriven_3 ? A_out : 1'bz;  // Controlled_Buffer controlled_buffer_11
  Button F (.out(F_out));
  assign controlled_buffer_4_out = undriven_3 ? E_out : 1'bz;  // Controlled_Buffer controlled_buffer_12
  assign controlled_buffer_1_out = undriven_4 ? _3_out : 1'bz;  // Controlled_Buffer controlled_buffer_13
  assign controlled_buffer_2_out = undriven_4 ? _7_out : 1'bz;  // Controlled_Buffer controlled_buffer_14
  assign controlled_buffer_3_out = undriven_4 ? B_out : 1'bz;  // Controlled_Buffer controlled_buffer_15
  assign controlled_buffer_4_out = undriven_4 ? F_out : 1'bz;  // Controlled_Buffer controlled_buffer_16
  Multiplexer multiplexer_1 (
    .in0(controlled_buffer_2_out), .in1(controlled_buffer_3_out), .out(multiplexer_1_out));  // open: sel, en
  Decoder decoder_1 (.out0(decoder_1_out0), .out1(decoder_1_out1));  // open: sel, en
  Multiplexer multiplexer_2 (.in0(undriven_3), .in1(undriven_2), .out(multiplexer_2_out));  // open: sel, en
  Decoder decoder_2 (.out1(decoder_2_out1));  // open: out0, sel, en
  not not_1 (not_1_out, decoder_1_out1);
  and and_1 (and_1_out, decoder_1_out0, not_1_out);
  or or_1 (and_1_out, decoder_1_out1, decoder_2_out1);
  Comparator comparator_1 (
    .a({undriven_5, Input_code}), .b({undriven_6, Predefined_code}), .gt(comparator_1_gt),
    .lt(comparator_1_lt));  // open: eq
  Demultiplexer #(.select(2)) demultiplexer_1 (
    .out0(demultiplexer_1_out0), .out1(demultiplexer_1_out1), .out2(demultiplexer_1_out2),
    .out3(demultiplexer_1_out3), .in(multiplexer_3_out), .sel(decoder_3_out1), .en(decoder_3_out0));
  Multiplexer multiplexer_3 (.in0(comparator_1_gt), .in1(comparator_1_lt), .out(multiplexer_3_out));  // open: sel, en
  Decoder decoder_3 (.out0(decoder_3_out0), .out1(decoder_3_out1[0]));  // open: sel, en
  LED led_1 (.in(demultiplexer_1_out0));
  LED led_2 (.in(demultiplexer_1_out1));
  LED led_3 (.in(demultiplexer_1_out2));
  LED led_4 (.in(demultiplexer_1_out3));
  // Pins of 1 and 2 bits meet at decoder_3_out1
  // Pins of 4 and 8 bits meet at {undriven_6, Predefined_code}
  // Pins of 4 and 8 bits meet at {undriven_5, Input_code}

  // Notes on the sheet:
  //   Door 1
  //   Door 2
  //   Door 3
  //   Door 4
endmodule
